# Fritzing sketch JukeboxWiring (saved by Fritzing 0.9.3b)
breadboards: 1

parts:
  Raspberry_Pi_1 = Raspberry Pi 4 [part_number=RPI-4-b]
  LED1 = LED - 5mm [color="Red (633nm)" package="5 mm [THT]"]
  S1 = Pushbutton [package="[THT]"]
  S2 = Pushbutton [package="[THT]"]
  S3 = Pushbutton [package="[THT]"]
  S4 = Pushbutton [package="[THT]"]
  S5 = Pushbutton [package="[THT]"]
  S6 = Pushbutton [package="[THT]"]

nets:
  N1: Raspberry_Pi_1.GPIO3, S1.Pin_3, S1.Pin_4
  N2: Raspberry_Pi_1.GPIO4, S2.Pin_3, S2.Pin_4
  N3: Raspberry_Pi_1.GPIO17, S3.Pin_3, S3.Pin_4
  N4: Raspberry_Pi_1.GPIO27, S4.Pin_3, S4.Pin_4
  N5: Raspberry_Pi_1.GPIO22, LED1.anode
  N6: Raspberry_Pi_1.GPIO5, S5.Pin_3, S5.Pin_4
  N7: Raspberry_Pi_1.GPIO6, S6.Pin_3, S6.Pin_4
  N8: Raspberry_Pi_1.GND, LED1.cathode, S1.Pin_1, S1.Pin_2, S2.Pin_1, S2.Pin_2, S3.Pin_1, S3.Pin_2, S4.Pin_1, S4.Pin_2, S5.Pin_1, S5.Pin_2, S6.Pin_1, S6.Pin_2

custom parts:
  Raspberry Pi 4: The RPi4, a faster version of the awesome Raspberry Pi 2 B ARM Board with 40 pin gpio. Ready for special Raspberry Pi B+ and RPi2 Hat (Hardware attached (on) top)
