# Fritzing sketch RaspberryPeripherals (saved by Fritzing 0.9.3b)
breadboards: 1

parts:
  Raspberry_Pi_1 = Raspberry Pi 4 [part_number=RPI-4-b]
  LED1 = LED - 5mm [color="Red (633nm)" package="5 mm [THT]"]
  S1 = Pushbutton [package="[THT]"]
  KY-1 = Keyes Relay [package=THT]
  M2 = DC Motor

nets:
  3V3: Raspberry_Pi_1.3v3, Raspberry_Pi_1.3V3, KY-1.power, KY-1.C
  N1: Raspberry_Pi_1.GPIO3, S1.Pin_3, S1.Pin_4
  N2: Raspberry_Pi_1.GPIO22, LED1.anode
  N3: Raspberry_Pi_1.GND, LED1.cathode, S1.Pin_1, S1.Pin_2, KY-1.ground, M2.pin_1
  N4: Raspberry_Pi_1.GPIO25, KY-1.signal
  N5: KY-1.NO, M2.pin_2

custom parts:
  Raspberry Pi 4: The RPi4, a faster version of the awesome Raspberry Pi 2 B ARM Board with 40 pin gpio. Ready for special Raspberry Pi B+ and RPi2 Hat (Hardware attached (on) top)
  Keyes Relay: The Keyes 5V relay module is suitable for SCM development, home appliance control. It uses a 5V~12V TIL control signal which can control DC / AC signal.
